// Logisim project CPU.circ as structural Verilog: 4 circuits, main circuit main
module main (
  input  RESET
);

  wire BCONST, C, CLK, Cn, DIVZ, FL_WE, HALTED, HI_WE, IND, IR_WE, MW_EN, N, or_1_out, or_2_out, or_3_out,
       or_4_out, PC_WE, PH, RW_EN, T0, T1, TAKEN, V, Z;
  wire [2:0] WSEL;
  wire [3:0] A, ALUOP, B, BALU, FLAGIN, HI, HIN, multiplexer_3_out, multiplexer_5_out, RAMD, regfile_1_r0,
       regfile_1_r1, regfile_1_r2, regfile_1_r3, WD, Y;
  wire [4:0] ADDR, bit_extender_1_out, RAMA;
  wire [6:0] INCPC, multiplexer_2_out, PC, PCIN;
  wire [11:0] multiplexer_4_out, ROMW;
  wire [11:5] IR;

  Clock u_CLK (.out(CLK));
  ROM #(.addrWidth(7), .dataWidth(12)) ProgramROM (.addr(PC), .data(ROMW));
  CONTROL control_1 (
    .CLK(CLK), .RESET(RESET), .OPC(IR[11:7]), .Z(Z), .C(C), .N(N), .DIVZ(DIVZ), .ALUOP(ALUOP), .WSEL(WSEL),
    .IND(IND), .BCONST(BCONST), .IR_WE(IR_WE), .PC_WE(PC_WE), .RW_EN(RW_EN), .HI_WE(HI_WE), .FL_WE(FL_WE),
    .MW_EN(MW_EN), .PH(PH), .HALTED(HALTED), .T0(T0), .T1(T1), .TAKEN(TAKEN));  // open: RW, MW, FW, HW
  REGFILE regfile_1 (
    .CLK(CLK), .RESET(RESET), .RD(IR[6:5]), .RS(ADDR[1:0]), .WD(WD), .WE(RW_EN), .A(A), .B(B),
    .R0(regfile_1_r0), .R1(regfile_1_r1), .R2(regfile_1_r2), .R3(regfile_1_r3));
  // Probe on regfile_1_r1
  // Probe on regfile_1_r3
  Adder #(.width(7)) adder_1 (.a(PC), .b(7'b0000001), .out(INCPC));  // open: cin, cout
  Multiplexer #(.width(7)) multiplexer_1 (.in0(INCPC), .in1({IR[6:5], ADDR}), .out(PCIN), .sel(PH));
  // Probe on regfile_1_r0
  // Probe on regfile_1_r2
  or or_1 (or_1_out, PC_WE, RESET);
  Multiplexer #(.width(7)) multiplexer_2 (.in0(PCIN), .in1({7{1'b0}}), .out(multiplexer_2_out), .sel(RESET));
  or or_2 (or_2_out, IR_WE, RESET);
  Multiplexer #(.width(4)) multiplexer_3 (.in0(HIN), .in1(4'b0000), .out(multiplexer_3_out), .sel(RESET));
  Register #(.width(7)) u_PC (.D(multiplexer_2_out), .en(or_1_out), .clk(CLK), .Q(PC), .clr(1'b0));
  ALU alu_1 (
    .A(A), .B(BALU), .OP(ALUOP), .K(ADDR[1:0]), .CF(C), .Y(Y), .HIN(HIN), .Z(FLAGIN[0]), .C(Cn),
    .N(FLAGIN[2]), .V(FLAGIN[3]), .DIVZ(DIVZ));
  Multiplexer #(.width(12)) multiplexer_4 (.in0(ROMW), .in1({12{1'b0}}), .out(multiplexer_4_out), .sel(RESET));
  Register #(.width(12)) u_IR (.D(multiplexer_4_out), .en(or_2_out), .clk(CLK), .Q({IR, ADDR}), .clr(1'b0));
  or or_3 (or_3_out, HI_WE, RESET);
  Register #(.width(4)) u_HI (.D(multiplexer_3_out), .en(or_3_out), .clk(CLK), .Q(HI), .clr(1'b0));
  Multiplexer #(.width(4)) multiplexer_5 (
    .in0({FLAGIN[3:2], Cn, FLAGIN[0]}), .in1(4'b0000), .out(multiplexer_5_out), .sel(RESET));
  RAM #(.addrWidth(5), .clearpin("true"), .dataWidth(4), .trigger("falling")) DataRAM (
    .addr(RAMA), .we(MW_EN), .oe(1'b1), .clk(CLK), .din(A), .dout(RAMD), .clr(1'b0));
  or or_4 (or_4_out, FL_WE, RESET);
  Register #(.width(4)) FLAGS (.D(multiplexer_5_out), .en(or_4_out), .clk(CLK), .Q({V, N, C, Z}), .clr(1'b0));
  Multiplexer #(.width(4)) multiplexer_6 (.in0(B), .in1(4'b0001), .out(BALU), .sel(BCONST));
  Multiplexer #(.select(3), .width(4)) multiplexer_7 (
    .in0(Y), .in1(RAMD), .in2(ADDR[3:0]), .in3(B), .in4(HI), .in5(4'b0000), .in6(4'b0000), .in7(4'b0000),
    .out(WD), .sel(WSEL));
  assign bit_extender_1_out = {{1{1'b0}}, B};  // Bit_Extender bit_extender_1
  Multiplexer #(.width(5)) multiplexer_8 (.in0(ADDR), .in1(bit_extender_1_out), .out(RAMA), .sel(IND));

  // Other names for the same wires on the sheet: Zn = FLAGIN[0]; FLAGIN[1] = Cn; Nn = FLAGIN[2]; Vn = FLAGIN[3];
  //   IMM[3:0] = ADDR[3:0]; IR[4:0] = ADDR; RS[1:0] = ADDR[1:0]; TGT[6:0] = {IR[6:5], ADDR}; RD[1:0] = IR[6:5];
  //   OPC[4:0] = IR[11:7]

  // Notes on the sheet:
  //   contents of ProgramROM (hex, n*v repeats v):
  //   180 1a8 1c4 361 803 6a0 740 503 11d f80
  //   this mux to change pc to pc+1 or jump target
  //   increment pc
  //   0 on reset else flagin when flag_enable
  //   b or 1 (in the case of inc or dec)
  //   This ram is to store nibbles
  //   this mux chooses the data written into a reg : Y, Ram, imm, b, HI
  //   choose direct address (addr) or register indirect address
endmodule

module ALU (
  input  [3:0] A,
  input  [3:0] B,
  input  [3:0] OP,
  input  [1:0] K,
  input  CF,
  output [3:0] Y,
  output [3:0] HIN,
  output Z,
  output C,
  output N,
  output V,
  output DIVZ
);

  wire and_5_out, and_6_out, CADD, CIN, D1, D2, D3, D4, D14, HNZ, or_1_out, SC, SUBM, VADD, xnor_1_out,
       xor_3_out, YZ;
  wire [3:0] AN, BDIV, BP, MASK, NT, ORR, PH, PL, Q, REM_t, ROLY, RORY, S, SHLH, SHLL, SHRH, SHRY, SUBM4, XR;

  or or_1 (or_1_out, ~D4, ~HNZ);  // OR_Gate
  or or_2 (SUBM, D2, D3, D14);
  assign SUBM4 = {{3{SUBM}}, SUBM};  // Bit_Extender bit_extender_1
  Decoder #(.enable("false"), .select(4)) decoder_1 (
    .out1(D1), .out2(D2), .out3(D3), .out4(D4), .out14(D14), .sel(OP));  // open: out0, out5, out6, out7, out8, out9, out10, out11, out12, out13, out15
  assign BP = B ^ SUBM4;  // XOR_Gate xor_1, 4 bits wide
  nor nor_1 (DIVZ, BP[0], BP[1], BP[2], BP[3]);
  and and_1 (Z, or_1_out, YZ);
  nor nor_2 (YZ, Y[0], Y[1], Y[2], N);
  Multiplexer #(.select(4), .width(4)) multiplexer_1 (
    .in0(4'b0000), .in1(4'b0000), .in2(4'b0000), .in3(4'b0000), .in4(PH), .in5(REM_t), .in6(4'b0000),
    .in7(4'b0000), .in8(4'b0000), .in9(4'b0000), .in10(SHLH), .in11(SHRH), .in12(4'b0000), .in13(4'b0000),
    .in14(4'b0000), .in15(4'b0000), .out(HIN), .sel(OP));
  Multiplier #(.width(4)) multiplier_1 (.a(A), .b(B), .out(PL), .cin(4'b0000), .cout(PH));
  Adder #(.width(4)) adder_1 (.a(A), .b(BP), .out(S), .cin(CIN), .cout(SC));
  Multiplexer #(.width(4)) multiplexer_2 (.in0(B), .in1(4'b0001), .out(BDIV), .sel(DIVZ));
  Divider #(.width(4)) divider_1 (.a(A), .b(BDIV), .out(Q), .upper(4'b0000), .rem(REM_t));
  or or_3 (HNZ, HIN[0], HIN[1], HIN[2], HIN[3]);
  Multiplexer #(.select(4), .width(4)) multiplexer_3 (
    .in0(S), .in1(S), .in2(S), .in3(S), .in4(PL), .in5(Q), .in6(AN), .in7(ORR), .in8(XR), .in9(NT),
    .in10(SHLL), .in11(SHRY), .in12(ROLY), .in13(RORY), .in14(S), .in15(S), .out({N, Y[2:0]}), .sel(OP));
  xor xor_2 (CADD, SUBM, SC);
  Multiplexer #(.select(2), .width(4)) multiplexer_4 (
    .in0(4'b0000), .in1(4'b0001), .in2(4'b0011), .in3(4'b0111), .out(MASK), .sel(K));
  assign SHRH = A & MASK;  // AND_Gate and_2, 4 bits wide
  assign AN = A & B;  // AND_Gate and_3, 4 bits wide
  assign ORR = A | B;  // OR_Gate or_4, 4 bits wide
  xnor xnor_1 (xnor_1_out, A[3], BP[3]);
  xor xor_3 (xor_3_out, A[3], S[3]);
  and and_4 (VADD, xnor_1_out, xor_3_out);
  Multiplexer #(.select(4)) multiplexer_5 (
    .in0(CADD), .in1(CADD), .in2(CADD), .in3(CADD), .in4(HNZ), .in5(1'b0), .in6(1'b0), .in7(1'b0),
    .in8(1'b0), .in9(1'b0), .in10(HNZ), .in11(HNZ), .in12(1'b0), .in13(1'b0), .in14(CADD), .in15(1'b0),
    .out(C), .sel(OP));
  and and_5 (and_5_out, D1, CF);
  and and_6 (and_6_out, D3, ~CF);  // AND_Gate
  Shifter #(.shift("lr"), .width(4)) shifter_1 (.in(A), .\dist (K), .out(SHRY));
  Shifter #(.shift("rl"), .width(4)) shifter_2 (.in(A), .\dist (K), .out(ROLY));
  Shifter #(.shift("rr"), .width(4)) shifter_3 (.in(A), .\dist (K), .out(RORY));
  assign XR = A ^ B;  // XOR_Gate xor_4, 4 bits wide
  assign NT = ~A;  // NOT_Gate not_1, 4 bits wide
  Shifter shifter_4 (.in({4'b0000, A}), .\dist ({1'b0, K}), .out({SHLH, SHLL}));
  Multiplexer #(.select(4)) multiplexer_6 (
    .in0(VADD), .in1(VADD), .in2(VADD), .in3(VADD), .in4(HNZ), .in5(DIVZ), .in6(1'b0), .in7(1'b0),
    .in8(1'b0), .in9(1'b0), .in10(HNZ), .in11(1'b0), .in12(1'b0), .in13(1'b0), .in14(VADD), .in15(1'b0),
    .out(V), .sel(OP));
  or or_5 (CIN, and_5_out, and_6_out, D2, D14);

  assign Y[3] = N;

  // Notes on the sheet:
  //   ADD: 0
  //   SUB: 2
  //   MUL: 4
  //   DIV: 5
  //   AND: 6
  //   OR: 7
  //   XOR: 8
  //   NOT: 9
  //   SHL: 10
  //   SHR: 11
  //   ROL: 12
  //   ROR: 13
endmodule

module REGFILE (
  input  CLK,
  input  RESET,
  input  [1:0] RD,
  input  [1:0] RS,
  input  [3:0] WD,
  input  WE,
  output [3:0] A,
  output [3:0] B,
  output [3:0] R0,
  output [3:0] R1,
  output [3:0] R2,
  output [3:0] R3
);

  wire L0, L1, L2, L3, or_1_out, or_2_out, or_3_out, or_4_out;
  wire [3:0] WDR;

  or or_1 (or_1_out, L0, RESET);
  or or_2 (or_2_out, L1, RESET);
  or or_3 (or_3_out, L2, RESET);
  or or_4 (or_4_out, L3, RESET);
  Multiplexer #(.width(4)) multiplexer_1 (.in0(WD), .in1(4'b0000), .out(WDR), .sel(RESET));
  Register #(.width(4)) register_1 (.D(WDR), .en(or_1_out), .clk(CLK), .Q(R0), .clr(1'b0));
  Register #(.width(4)) register_2 (.D(WDR), .en(or_2_out), .clk(CLK), .Q(R1), .clr(1'b0));
  Register #(.width(4)) register_3 (.D(WDR), .en(or_3_out), .clk(CLK), .Q(R2), .clr(1'b0));
  Register #(.width(4)) register_4 (.D(WDR), .en(or_4_out), .clk(CLK), .Q(R3), .clr(1'b0));
  Decoder #(.select(2)) decoder_1 (.out0(L0), .out1(L1), .out2(L2), .out3(L3), .sel(RD), .en(WE));
  Multiplexer #(.select(2), .width(4)) multiplexer_2 (.in0(R0), .in1(R1), .in2(R2), .in3(R3), .out(A), .sel(RD));
  Multiplexer #(.select(2), .width(4)) multiplexer_3 (.in0(R0), .in1(R1), .in2(R2), .in3(R3), .out(B), .sel(RS));

  // Notes on the sheet:
  //   when write enable is  1; turn the dest number into one line enable
endmodule

module CONTROL (
  input  CLK,
  input  RESET,
  input  [4:0] OPC,
  input  Z,
  input  C,
  input  N,
  input  DIVZ,
  output [3:0] ALUOP,
  output [2:0] WSEL,
  output RW,
  output MW,
  output IND,
  output BCONST,
  output FW,
  output HW,
  output IR_WE,
  output PC_WE,
  output RW_EN,
  output HI_WE,
  output FL_WE,
  output MW_EN,
  output PH,
  output HALTED,
  output T0,
  output T1,
  output TAKEN
);

  wire and_1_out, and_7_out, and_8_out, and_9_out, and_10_out, and_11_out, and_14_out, and_15_out, B1, B2,
       B3, B4, B5, comparator_1_eq, DIVG, HALTCW, or_2_out, xnor_1_out;
  wire [2:0] BR;

  Comparator #(.width(4)) comparator_1 (.a(ALUOP), .b(4'b0101), .eq(comparator_1_eq));  // open: gt, lt
  and and_1 (and_1_out, T1, TAKEN);
  and and_2 (RW_EN, T1, RW, ~DIVG);  // AND_Gate
  and and_3 (HI_WE, T1, HW, ~DIVG);  // AND_Gate
  and and_4 (FL_WE, T1, FW);
  and and_5 (MW_EN, T1, MW);
  and and_6 (DIVG, DIVZ, comparator_1_eq);
  or or_1 (PC_WE, IR_WE, and_1_out);
  ROM #(.addrWidth(5), .dataWidth(17)) ControlROM (
    .addr(OPC), .data({HALTCW, BR, BCONST, IND, HW, FW, MW, WSEL, RW, ALUOP}));
  and and_7 (and_7_out, Z, B2);
  and and_8 (and_8_out, ~Z, B3);  // AND_Gate
  and and_9 (and_9_out, C, B4);
  and and_10 (and_10_out, N, B5);
  xnor xnor_1 (xnor_1_out, PH, HALTED);
  or or_2 (or_2_out, HALTED, and_11_out);
  and and_11 (and_11_out, PH, HALTCW);
  and and_12 (IR_WE, ~PH, ~HALTED);  // AND_Gate
  and and_13 (T1, PH, ~HALTED);  // AND_Gate
  Decoder #(.enable("false"), .select(3)) decoder_1 (
    .out1(B1), .out2(B2), .out3(B3), .out4(B4), .out5(B5), .sel(BR));  // open: out0, out6, out7
  and and_14 (and_14_out, ~RESET, xnor_1_out);  // AND_Gate
  and and_15 (and_15_out, ~RESET, or_2_out);  // AND_Gate
  or or_3 (TAKEN, B1, and_7_out, and_8_out, and_9_out, and_10_out);
  D_Flip_Flop d_ff_1 (.D(and_14_out), .clk(CLK), .Q(PH));  // open: Qn, preset, reset
  D_Flip_Flop d_ff_2 (.D(and_15_out), .clk(CLK), .Q(HALTED));  // open: Qn, preset, reset

  assign T0 = IR_WE;

  // Notes on the sheet:
  //   divide by zero guard
  //   contents of ControlROM (hex, n*v repeats v):
  //   0 30 100 50 70 90 830 900 2000 4000 6000 8000 a000 1210 1212 0 210 211 212 213 614 615 216 217 218
  //   219 61a 61b 21c 21d 20e 10000
  //   truth table of CPU, one word per opcode
  //   Fetch or Execute
  //   freeze the machine
  //   these two are responsible for branch and loops
endmodule
