// Logisim project Lock.circ as structural Verilog: 10 circuits, main circuit MAIN
module MAIN (
  input  RESET,
  input  ENTER,
  input  CLEAR,
  input  [3:0] DIGIT
);

  wire CLK_out, door_lock_1_fail, door_lock_1_invalid, door_lock_1_lockout, door_lock_1_unlock;
  wire [1:0] door_lock_1_attempts, door_lock_1_digits_entered;
  wire [3:0] bit_extender_1_out, bit_extender_2_out;

  Clock CLK (.out(CLK_out));
  DOOR_LOCK door_lock_1 (
    .CLK(CLK_out), .RESET(RESET), .ENTER(ENTER), .CLEAR(CLEAR), .DIGIT(DIGIT), .INVALID(door_lock_1_invalid),
    .FAIL(door_lock_1_fail), .ATTEMPTS(door_lock_1_attempts), .DIGITS_ENTERED(door_lock_1_digits_entered),
    .LOCKOUT(door_lock_1_lockout), .UNLOCK(door_lock_1_unlock));
  LED led_1 (.in(door_lock_1_invalid));
  LED led_2 (.in(door_lock_1_fail));
  LED led_3 (.in(door_lock_1_lockout));
  LED led_4 (.in(door_lock_1_unlock));
  assign bit_extender_1_out = {{2{1'b0}}, door_lock_1_attempts};  // Bit_Extender bit_extender_1
  assign bit_extender_2_out = {{2{1'b0}}, door_lock_1_digits_entered};  // Bit_Extender bit_extender_2
  Hex_Digit_Display #(.decimalPoint("false")) ATTEMPTS (.value(bit_extender_1_out));
  Hex_Digit_Display #(.decimalPoint("false")) DIGIT_ENTERED (.value(bit_extender_2_out));
endmodule

module EDGE_DETECT (
  input  BTN,
  input  CLK,
  output EV,
  output PREV
);

  wire not_1_out;

  D_Flip_Flop d_ff_1 (.D(BTN), .clk(CLK), .Q(PREV));  // open: Qn, preset, reset
  not not_1 (not_1_out, PREV);
  and and_1 (EV, BTN, not_1_out);

  // Notes on the sheet:
  //   PREV: Previous button value
  //   EV: Detect if a button is activated which was previously not
endmodule

module EVENT_LOGIC (
  input  RUN,
  input  RESET,
  input  S1,
  input  S0,
  input  CLR_EV,
  input  ENT_EV,
  input  [3:0] DIGIT,
  output EN,
  output IN_ENTRY,
  output IN_UNL,
  output DO_CLEAR,
  output VALID_ENT,
  output INV_ENT
);

  wire DO_ENTER, INV, or_1_out;

  and and_1 (EN, RUN, ~RESET);  // AND_Gate
  or or_1 (or_1_out, DIGIT[1], DIGIT[2]);
  nor nor_1 (IN_ENTRY, S1, S0);
  and and_2 (IN_UNL, ~S1, S0);  // AND_Gate
  and and_3 (INV, or_1_out, DIGIT[3]);
  and and_4 (DO_CLEAR, EN, IN_ENTRY, CLR_EV);
  and and_5 (DO_ENTER, EN, ~CLR_EV, ENT_EV, IN_ENTRY);  // AND_Gate
  and and_6 (VALID_ENT, DO_ENTER, ~INV);  // AND_Gate
  and and_7 (INV_ENT, DO_ENTER, INV);

  // Notes on the sheet:
  //   S : 00 :  IN ENTRY
  //   01 : UNCLOCKED
  //   10 : LOCKED
  //   CLR_EV : Clear Event
  //   ENT_EV : Enter Event
  //   EN : Running and not Reset
  //   DO_CLEAR : Clear event and in entry
  //   INV : Invalid digits (10-15)
  //   VALID_ENT : Valid entry
  //   INV_ENT : Invalid Entry
  //   DO_ENTER : Enter event and in entry
endmodule

module RESULT_LOGIC (
  input  [1:0] CNT,
  input  VALID_ENT,
  input  MATCH,
  input  [1:0] ATT,
  output C_IS0,
  output C_IS3,
  output LD1,
  output LD2,
  output LD3,
  output COMPLETE,
  output CORRECT,
  output WRONG,
  output LOCK3
);

  wire C_IS1, C_IS2;

  Decoder #(.select(2)) decoder_1 (.out0(C_IS0), .out1(C_IS1), .out2(C_IS2), .out3(C_IS3), .sel(CNT));  // open: en
  and and_1 (LD1, C_IS0, VALID_ENT);
  and and_2 (LD2, C_IS1, VALID_ENT);
  and and_3 (LD3, C_IS2, VALID_ENT);
  and and_4 (COMPLETE, VALID_ENT, C_IS3);
  and and_5 (CORRECT, MATCH, COMPLETE);
  and and_6 (WRONG, COMPLETE, ~MATCH);  // AND_Gate
  and and_7 (LOCK3, WRONG, ~ATT[0], ATT[1]);  // AND_Gate

  // Notes on the sheet:
  //   CNT : No. of digits entered
  //   ATT :  No. of attempts
  //   VALID_ENT : from EVENT_LOGIC
  //   MATCH : from PIN_COMPARE
  //   C_IS[0:3] : Counter Position Indicators
  //   LD[1:3] : Load ith character
  //   CORRECT : Complete and Match
  //   WRONG : Complete and not Match
  //   LOCK3 : Lock out after 3rd failure
  //   COMPLETE : Indicates final digit has been entered
endmodule

module PIN_COMPARE (
  input  [3:0] R1,
  input  [3:0] R2,
  input  [3:0] R3,
  input  [3:0] DIGIT,
  output MATCH
);

  wire comparator_1_eq, comparator_2_eq, comparator_3_eq, comparator_4_eq;

  Comparator #(.width(4)) comparator_1 (.a(4'b0010), .b(R1), .eq(comparator_1_eq));  // open: gt, lt
  Comparator #(.width(4)) comparator_2 (.a(4'b0100), .b(R2), .eq(comparator_2_eq));  // open: gt, lt
  Comparator #(.width(4)) comparator_3 (.a(4'b0110), .b(R3), .eq(comparator_3_eq));  // open: gt, lt
  Comparator #(.width(4)) comparator_4 (.a(4'b1000), .b(DIGIT), .eq(comparator_4_eq));  // open: gt, lt
  and and_1 (MATCH, comparator_1_eq, comparator_2_eq, comparator_3_eq, comparator_4_eq);
endmodule

module DIGIT_STORE (
  input  CLR_STORE,
  input  [3:0] DIGIT,
  input  LD1,
  input  LD2,
  input  CLK,
  input  LD3,
  output [3:0] R1,
  output [3:0] R2,
  output [3:0] R3
);

  wire or_1_out, or_2_out, or_3_out;
  wire [3:0] multiplexer_1_out;

  Multiplexer #(.width(4)) multiplexer_1 (.in0(DIGIT), .in1(4'b0000), .out(multiplexer_1_out), .sel(CLR_STORE));
  or or_1 (or_1_out, CLR_STORE, LD1);
  or or_2 (or_2_out, CLR_STORE, LD2);
  or or_3 (or_3_out, CLR_STORE, LD3);
  Register #(.width(4)) register_1 (.D(multiplexer_1_out), .en(or_1_out), .clk(CLK), .Q(R1), .clr(1'b0));
  Register #(.width(4)) register_2 (.D(multiplexer_1_out), .en(or_2_out), .clk(CLK), .Q(R2), .clr(1'b0));
  Register #(.width(4)) register_3 (.D(multiplexer_1_out), .en(or_3_out), .clk(CLK), .Q(R3), .clr(1'b0));
endmodule

module COUNTERS (
  input  RESET,
  input  CORRECT,
  input  CLK,
  input  WRONG,
  input  VALID_ENT,
  input  DO_CLEAR,
  input  C_IS3,
  input  COMPLETE,
  input  C_IS0,
  output [1:0] CNT,
  output [1:0] ATT,
  output CLR_STORE,
  output FAIL
);

  wire and_1_out, and_2_out, and_3_out, CLR_ATT, CLR_FAIL, or_1_out, or_2_out, or_3_out;
  wire [1:0] adder_1_out, adder_2_out, multiplexer_1_out, multiplexer_2_out;

  or or_1 (or_1_out, FAIL, WRONG);
  and and_1 (and_1_out, C_IS0, VALID_ENT);
  and and_2 (and_2_out, ~CLR_FAIL, or_1_out);  // AND_Gate
  and and_3 (and_3_out, VALID_ENT, ~C_IS3);  // AND_Gate
  or or_2 (or_2_out, and_3_out, CLR_STORE);
  or or_3 (or_3_out, RESET, CORRECT, WRONG);
  or or_4 (CLR_FAIL, RESET, CORRECT, DO_CLEAR, and_1_out);
  D_Flip_Flop d_ff_1 (.D(and_2_out), .clk(CLK), .Q(FAIL));  // open: Qn, preset, reset
  Register #(.width(2)) CNT_REGISTER (.D(multiplexer_1_out), .en(or_2_out), .clk(CLK), .Q(CNT), .clr(1'b0));
  Register #(.width(2)) ATT_REGISTER (.D(multiplexer_2_out), .en(or_3_out), .clk(CLK), .Q(ATT), .clr(1'b0));
  Multiplexer #(.width(2)) multiplexer_1 (.in0(adder_1_out), .in1(2'b00), .out(multiplexer_1_out), .sel(CLR_STORE));
  Multiplexer #(.width(2)) multiplexer_2 (.in0(adder_2_out), .in1(2'b00), .out(multiplexer_2_out), .sel(CLR_ATT));
  or or_5 (CLR_ATT, RESET, CORRECT);
  Adder #(.width(2)) adder_1 (.a(CNT), .b(2'b01), .out(adder_1_out), .cin(1'b0));  // open: cout
  Adder #(.width(2)) adder_2 (.a(ATT), .b(2'b01), .out(adder_2_out), .cin(1'b0));  // open: cout
  or or_6 (CLR_STORE, RESET, DO_CLEAR, COMPLETE);

  // Notes on the sheet:
  //   CNT : Displays the number of digits entered
  //   ATT : Displays the number of attempts
  //   FAIL : Gives the immediate feedback after one attempt
endmodule

module UNLOCK_TIMER (
  input  IN_UNL,
  input  RESET,
  input  CLK,
  output [8:0] TMR,
  output EXPIRE
);

  wire TMR_EQ, TMR_MASK;
  wire [8:0] adder_1_out, multiplexer_1_out;

  Multiplexer #(.width(9)) multiplexer_1 (.in0({9{1'b0}}), .in1(adder_1_out), .out(multiplexer_1_out), .sel(TMR_MASK));
  Register #(.width(9)) register_1 (.D(multiplexer_1_out), .en(1'b1), .clk(CLK), .Q(TMR), .clr(1'b0));
  and and_1 (EXPIRE, IN_UNL, TMR_EQ, ~RESET);  // AND_Gate
  and and_2 (TMR_MASK, IN_UNL, ~RESET, ~EXPIRE);  // AND_Gate
  Adder #(.width(9)) adder_1 (.a(TMR), .b(9'h1), .out(adder_1_out), .cin(1'b0));  // open: cout
  Comparator #(.width(9)) comparator_1 (.a(TMR), .b(9'h13f), .eq(TMR_EQ));  // open: gt, lt

  // Notes on the sheet:
  //   IN_UNL : Represents the state of locked / unlocked
  //   TMR : Current time after unlock (master period )
  //   TMR_EQ : Gets active when TMR equals master period 319
  //   EXPIRE : To expire current session when timer hits 319
endmodule

module STATE_REG (
  input  CLK,
  input  RESET,
  input  CORRECT,
  input  LOCK3,
  input  EXPIRE,
  input  IN_UNL,
  output S0,
  output S1,
  output UNLOCK,
  output LOCKOUT
);

  wire and_1_out, and_2_out, and_3_out, or_1_out, or_2_out;

  and and_1 (and_1_out, IN_UNL, ~EXPIRE);  // AND_Gate
  or or_1 (or_1_out, CORRECT, and_1_out);
  or or_2 (or_2_out, LOCK3, S1);
  and and_2 (and_2_out, ~RESET, or_1_out);  // AND_Gate
  and and_3 (and_3_out, ~RESET, or_2_out);  // AND_Gate
  and and_4 (UNLOCK, S0, ~S1);  // AND_Gate
  and and_5 (LOCKOUT, ~S0, S1);  // AND_Gate
  D_Flip_Flop S0_FF (.D(and_2_out), .clk(CLK), .Q(S0));  // open: Qn, preset, reset
  D_Flip_Flop S1_FF (.D(and_3_out), .clk(CLK), .Q(S1));  // open: Qn, preset, reset
endmodule

module DOOR_LOCK (
  input  CLK,
  input  RESET,
  input  ENTER,
  input  CLEAR,
  input  [3:0] DIGIT,
  output INVALID,
  output FAIL,
  output [1:0] ATTEMPTS,
  output [1:0] DIGITS_ENTERED,
  output LOCKOUT,
  output UNLOCK
);

  wire C_IS0, C_IS3, CLR_EV, CLR_STORE, COMPLETE, CORRECT, DO_CLEAR, EN, ENT_EV, EXPIRE, IN_ENTRY, IN_UNL,
       INV_ENT, LD1, LD2, LD3, LOCK3, MATCH, not_1_out, RUN, S0, S1, VALID_ENT, WRONG;
  wire [3:0] R1, R2, R3;
  wire [8:0] TMR;

  D_Flip_Flop d_ff_1 (.D(INV_ENT), .clk(CLK), .Q(INVALID));  // open: Qn, preset, reset
  not not_1 (not_1_out, RESET);
  D_Flip_Flop d_ff_2 (.D(not_1_out), .clk(CLK), .Q(RUN));  // open: Qn, preset, reset
  EDGE_DETECT edge_detect_1 (.BTN(ENTER), .CLK(CLK), .EV(ENT_EV));  // open: PREV
  EDGE_DETECT edge_detect_2 (.BTN(CLEAR), .CLK(CLK), .EV(CLR_EV));  // open: PREV
  EVENT_LOGIC event_logic_1 (
    .RUN(RUN), .RESET(RESET), .S1(S1), .S0(S0), .CLR_EV(CLR_EV), .ENT_EV(ENT_EV), .DIGIT(DIGIT), .EN(EN),
    .IN_ENTRY(IN_ENTRY), .IN_UNL(IN_UNL), .DO_CLEAR(DO_CLEAR), .VALID_ENT(VALID_ENT), .INV_ENT(INV_ENT));
  PIN_COMPARE pin_compare_1 (.R1(R1), .R2(R2), .R3(R3), .DIGIT(DIGIT), .MATCH(MATCH));
  RESULT_LOGIC result_logic_1 (
    .CNT(DIGITS_ENTERED), .VALID_ENT(VALID_ENT), .MATCH(MATCH), .ATT(ATTEMPTS), .C_IS0(C_IS0), .C_IS3(C_IS3),
    .LD1(LD1), .LD2(LD2), .LD3(LD3), .COMPLETE(COMPLETE), .CORRECT(CORRECT), .WRONG(WRONG), .LOCK3(LOCK3));
  DIGIT_STORE digit_store_1 (
    .CLR_STORE(CLR_STORE), .DIGIT(DIGIT), .LD1(LD1), .LD2(LD2), .CLK(CLK), .LD3(LD3), .R1(R1), .R2(R2),
    .R3(R3));
  COUNTERS counters_1 (
    .RESET(RESET), .CORRECT(CORRECT), .CLK(CLK), .WRONG(WRONG), .VALID_ENT(VALID_ENT), .DO_CLEAR(DO_CLEAR),
    .C_IS3(C_IS3), .COMPLETE(COMPLETE), .C_IS0(C_IS0), .CNT(DIGITS_ENTERED), .ATT(ATTEMPTS),
    .CLR_STORE(CLR_STORE), .FAIL(FAIL));
  UNLOCK_TIMER unlock_timer_1 (.IN_UNL(IN_UNL), .RESET(RESET), .CLK(CLK), .TMR(TMR), .EXPIRE(EXPIRE));
  STATE_REG state_reg_1 (
    .CLK(CLK), .RESET(RESET), .CORRECT(CORRECT), .LOCK3(LOCK3), .EXPIRE(EXPIRE), .IN_UNL(IN_UNL), .S0(S0),
    .S1(S1), .UNLOCK(UNLOCK), .LOCKOUT(LOCKOUT));

  // Other names for the same wires on the sheet: ATT[1:0] = ATTEMPTS; CNT[1:0] = DIGITS_ENTERED
endmodule
